// Logisim project 8bitcircuit.circ as structural Verilog: 3 circuits, main circuit main
module main (
  input  [7:0] a,
  input  [7:0] in_2,
  output [7:0] out_3,
  output overflow
);

  wire fulladders_1_carryout, fulladders_2_carryout, fulladders_3_carryout, fulladders_4_carryout,
       fulladders_5_carryout, fulladders_6_carryout, halfadder_1_carry;

  HalfAdder halfadder_1 (.a(a[0]), .b(in_2[0]), .sum(out_3[0]), .carry(halfadder_1_carry));
  FullAdders fulladders_1 (
    .carryin(halfadder_1_carry), .a(a[1]), .b(in_2[1]), .sum(out_3[1]), .carryout(fulladders_1_carryout));
  FullAdders fulladders_2 (
    .carryin(fulladders_1_carryout), .a(a[2]), .b(in_2[2]), .sum(out_3[2]), .carryout(fulladders_2_carryout));
  FullAdders fulladders_3 (
    .carryin(fulladders_2_carryout), .a(a[3]), .b(in_2[3]), .sum(out_3[3]), .carryout(fulladders_3_carryout));
  FullAdders fulladders_4 (
    .carryin(fulladders_3_carryout), .a(a[4]), .b(in_2[4]), .sum(out_3[4]), .carryout(fulladders_4_carryout));
  FullAdders fulladders_5 (
    .carryin(fulladders_4_carryout), .a(a[5]), .b(in_2[5]), .sum(out_3[5]), .carryout(fulladders_5_carryout));
  FullAdders fulladders_6 (
    .carryin(fulladders_5_carryout), .a(a[6]), .b(in_2[6]), .sum(out_3[6]), .carryout(fulladders_6_carryout));
  FullAdders fulladders_7 (.carryin(fulladders_6_carryout), .a(a[7]), .b(in_2[7]), .sum(out_3[7]), .carryout(overflow));
endmodule

module FullAdders (
  input  carryin,
  input  a,
  input  b,
  output sum,
  output carryout
);

  wire and_1_out, and_2_out, xor_1_out;

  xor xor_1 (xor_1_out, a, b);
  and and_1 (and_1_out, a, b);
  xor xor_2 (sum, carryin, xor_1_out);
  and and_2 (and_2_out, carryin, xor_1_out);
  or or_1 (carryout, and_2_out, and_1_out);
endmodule

module HalfAdder (
  input  a,
  input  b,
  output sum,
  output carry
);

  xor xor_1 (sum, a, b);
  and and_1 (carry, a, b);
endmodule
